// Digital circuit Processor.dig as structural Verilog
// Simple processor based on the MIPS architecture. 
// It is a Harvard single-cycle CPU.
// {{de Einfacher Prozessor, der an die MIPS-Architektur 
// angelehnt ist. Es handelt sich um eine Harvard 
// Single-Cycle CPU.}}
module Processor (
  input  Clock
);

  wire abs, alu2D, alu_1_carry, alu_1_neg, alu_1_zero, branch_1_jmp, flags_1_co, flags_1_no, flags_1_zo, imm,
       ioR, ioW, ld, muxA, RetI, sf, src2D, st, stPC, WE;
  wire [1:0] iem;
  wire [2:0] br, muxB;
  wire [4:0] aluOp;
  wire [15:0] alu_1_y, driver_1_out, imreg_1_imm, multiplexer_1_out, multiplexer_2_out, pc_1_next, pc_1_pc,
       register_1_rdest, register_1_rsrc, romdualport_1_d1, romdualport_1_d2, signext_1__5d, signext_1__5s,
       signext_1__9sd;

  PC pc_1 (.ALU(alu_1_y), .C(Clock), .abs(abs), .rel(branch_1_jmp), .Next(pc_1_next), .PC(pc_1_pc));
  ROMDualPort #(.AddrBits(16), .isProgramMemory("true"), .Bits(16)) romdualport_1 (
    .A1(register_1_rsrc), .s1(1'b1), .A2(pc_1_pc), .s2(1'b1), .D1(romdualport_1_d1), .D2(romdualport_1_d2));
  assign driver_1_out = stPC ? pc_1_next : 16'bz;  // Driver driver_1
  Control control_1 (
    .Op(romdualport_1_d2[15:8]), .stPC(stPC), .WE(WE), .imm(imm), .iem(iem), .absJmp(abs), .muxB(muxB),
    .src2D(src2D), .muxA(muxA), .alu2D(alu2D), .aluOp(aluOp), .storeFlags(sf), .branch(br), .ramSt(st),
    .ramLd(ld), .ioW(ioW), .ioR(ioR), .RetI(RetI));
  Register register_1 (
    .WD(driver_1_out), .C(Clock), .src(romdualport_1_d2[3:0]), .dest(romdualport_1_d2[7:4]), .WE(WE),
    .Rdest(register_1_rdest), .Rsrc(register_1_rsrc));
  ImReg imreg_1 (.en(imm), .iem(iem), .C(Clock), .inst(romdualport_1_d2), .imm(imreg_1_imm));
  SignExt signext_1 (.inst(romdualport_1_d2), ._5S(signext_1__5s), ._9SD(signext_1__9sd), ._5D(signext_1__5d));
  assign driver_1_out = src2D ? register_1_rsrc : 16'bz;  // Driver driver_2
  Multiplexer #(.Bits(16)) multiplexer_1 (
    .sel(muxA), .in_0(register_1_rdest), .in_1(register_1_rsrc), .out(multiplexer_1_out));
  Multiplexer #(.Selector_Bits(3), .Bits(16)) multiplexer_2 (
    .sel(muxB), .in_0(register_1_rsrc), .in_1(romdualport_1_d1), .in_2(imreg_1_imm), .in_3({16{1'b0}}),
    .in_4({16{1'b0}}), .in_5(signext_1__5s), .in_6(signext_1__9sd), .in_7(signext_1__5d),
    .out(multiplexer_2_out));
  Branch branch_1 (.Z(flags_1_zo), .N(flags_1_no), .C(flags_1_co), .ctrl(br), .jmp(branch_1_jmp));
  ALU alu_1 (
    .A(multiplexer_1_out), .B(multiplexer_2_out), .Op(aluOp), .Y(alu_1_y), .Zero(alu_1_zero),
    .Neg(alu_1_neg), .Carry(alu_1_carry), .Ci(flags_1_co));
  assign driver_1_out = alu2D ? alu_1_y : 16'bz;  // Driver driver_3
  Flags flags_1 (
    .Zi(alu_1_zero), .Ni(alu_1_neg), .Ci(alu_1_carry), .C(Clock), .store(sf), .Zo(flags_1_zo),
    .No(flags_1_no), .Co(flags_1_co));
  RAMSinglePort #(.AddrBits(16), .Bits(16), .Addr_Bits(16)) ramsingleport_1 (
    .A(alu_1_y), .str(st), .C(Clock), .ld(ld), .D(driver_1_out));
  Graphics graphics_1 (.A(alu_1_y), .R(ioR), .C(Clock), .W(ioW), .D(driver_1_out));
  Terminal terminal_1 (.D(driver_1_out), .A(alu_1_y), .C(Clock), .W(ioW));

  // Other names for the same wires on the sheet: C = Clock

  // Notes on the sheet:
  //   Clock: Hz: 2147483647
  //   contents of romdualport_1 (hex, n*v repeats v):
  //   8000,961,8190,951,a90,a83,a25,a3a,10e1,afc,2bef,3d5f,c21,212f,38f9,3d20,105,116,a30,
  //   a20,aa0,8035,3ac0,4380,2180,3505,2172,3505,2173,3503,3d03,2173,3801,aa3,401a,c01,
  //   c11,c21,8014,2020,38eb,c31,8014,2030,38e6,1991,ffff,3e09,146,165,154,4400,3ddb,a70,
  //   1031,8014,f00,8060,3ab0,c21,c01,8060,3ab0,c31,8014,b00,8060,3ab0,c31,8014,b00,8060,
  //   3ab0,1021,1001,8060,3ab0,1021,1001,8060,3ab0,1031,8014,f00,8060,3ab0,1031,8014,f00,
  //   8060,3ab0,c21,c31,8015,b00,3b0c,8014,2020,3707,8014,2030,3704,4380,2180,3501,c71,
  //   3b0b,143,8014,1c40,242,246,4048,2cfe,ce1,3b0f
endmodule
